// Logisim project 8_Bit_CPU.circ as structural Verilog: 1 circuit, main circuit main
module main (
  input  [3:0] in_1,
  input  [3:0] in_2,
  input  [3:0] Adress_Proram,
  input  Reset_computer,
  input  Program_Enable,
  input  [7:0] Memory_Program,
  input  [3:0] in_7,
  output [3:0] out_8
);

  wire clock_1_out, clock_2_out, controlled_buffer_1_out, controlled_buffer_2_out, controlled_buffer_5_out,
       controlled_buffer_14_out, controlled_buffer_16_out, decoder_1_out5, not_1_out, not_2_out, not_3_out,
       not_4_out, not_5_out, subtractor_1_bout, xor_1_out;
  wire [1:0] nor_1_out, register_3_q;
  wire [2:0] counter_1_q;
  wire [3:0] Memory_adress_Registor_q, multiplexer_2_out, rom_2_data, rom_3_data, rom_4_data;
  wire [7:0] adder_1_out, controlled_buffer_7_out, Instruction_Registor_q, multiplexer_1_out,
       multiplexer_3_out, OutPut_Reg_q, ram_1_dout, register_1_q, register_2_q, subtractor_1_out;
  wire [17:0] rom_1_data;

  Clock clock_1 (.out(clock_1_out));
  not not_1 (not_1_out, Program_Enable);
  assign controlled_buffer_1_out = Reset_computer ? Reset_computer : 1'bz;  // Controlled_Buffer controlled_buffer_1
  Counter #(.max('h7), .width(3)) counter_1 (
    .clr(controlled_buffer_1_out), .clk(not_3_out), .Q(counter_1_q));  // open: load, up, count, D, carry
  assign controlled_buffer_2_out = not_1_out ? rom_1_data[11] : 1'bz;  // Controlled_Buffer controlled_buffer_2
  not not_2 (not_2_out, Reset_computer);
  assign controlled_buffer_1_out = not_2_out ? decoder_1_out5 : 1'bz;  // Controlled_Buffer controlled_buffer_3
  assign controlled_buffer_2_out = Program_Enable ? Program_Enable : 1'bz;  // Controlled_Buffer controlled_buffer_4
  assign controlled_buffer_5_out = Program_Enable ? Program_Enable : 1'bz;  // Controlled_Buffer controlled_buffer_5
  assign controlled_buffer_5_out = not_1_out ? rom_1_data[13] : 1'bz;  // Controlled_Buffer controlled_buffer_6
  xor xor_1 (xor_1_out, clock_1_out, Program_Enable);
  Multiplexer #(.width(8)) multiplexer_1 (
    .in0(controlled_buffer_7_out), .in1(Memory_Program), .out(multiplexer_1_out), .sel(Program_Enable));
  Counter #(.max('hf), .width(4)) counter_2 (
    .clr(Reset_computer), .load(rom_1_data[14]), .count(rom_1_data[15]), .clk(controlled_buffer_16_out),
    .D(controlled_buffer_7_out[3:0]), .Q(out_8));  // open: up, carry
  RAM #(.addrWidth(4)) ram_1 (
    .addr(Memory_adress_Registor_q), .we(controlled_buffer_5_out), .clk(clock_1_out),
    .din(multiplexer_1_out), .dout(ram_1_dout));  // open: oe
  not not_3 (not_3_out, controlled_buffer_16_out);
  Decoder #(.select(3)) decoder_1 (
    .out5(decoder_1_out5), .sel(counter_1_q));  // open: out0, out1, out2, out3, out4, out6, out7, en
  Register #(.width(4)) Memory_adress_Registor (
    .D(multiplexer_2_out), .en(controlled_buffer_2_out), .clk(xor_1_out), .Q(Memory_adress_Registor_q),
    .clr(Reset_computer));
  Multiplexer #(.width(4)) multiplexer_2 (
    .in0(controlled_buffer_7_out[3:0]), .in1(Adress_Proram), .out(multiplexer_2_out), .sel(Program_Enable));
  ROM #(.addrWidth(9), .dataWidth(18)) rom_1 (
    .addr({register_3_q, counter_1_q, Instruction_Registor_q[7:4]}), .data(rom_1_data));
  Register Instruction_Registor (
    .D(controlled_buffer_7_out), .en(rom_1_data[9]), .clk(controlled_buffer_16_out),
    .Q(Instruction_Registor_q), .clr(Reset_computer));
  assign controlled_buffer_7_out[3:0] = rom_1_data[16] ? out_8 : 4'bz;  // Controlled_Buffer controlled_buffer_7
  assign controlled_buffer_7_out[3:0] = rom_1_data[10] ? Memory_adress_Registor_q : 4'bz;  // Controlled_Buffer controlled_buffer_8
  assign controlled_buffer_7_out = rom_1_data[12] ? ram_1_dout : 8'bz;  // Controlled_Buffer controlled_buffer_9
  assign controlled_buffer_7_out[7:4] = rom_1_data[16] ? in_1 : 4'bz;  // Controlled_Buffer controlled_buffer_10
  assign controlled_buffer_7_out[7:4] = rom_1_data[10] ? in_2 : 4'bz;  // Controlled_Buffer controlled_buffer_11
  assign controlled_buffer_7_out[3:0] = rom_1_data[8] ? Instruction_Registor_q[3:0] : 4'bz;  // Controlled_Buffer controlled_buffer_12
  assign controlled_buffer_7_out[7:4] = rom_1_data[8] ? in_7 : 4'bz;  // Controlled_Buffer controlled_buffer_13
  Hex_Digit_Display #(.decimalPoint("false")) hex_digit_display_1 (.value(controlled_buffer_7_out[7:4]));
  Clock #(.highDuration(2), .lowDuration(2)) clock_2 (.out(clock_2_out));
  Hex_Digit_Display #(.decimalPoint("false")) hex_digit_display_2 (.value(controlled_buffer_7_out[3:0]));
  not not_4 (not_4_out, Program_Enable);
  assign controlled_buffer_14_out = not_4_out ? rom_1_data[7] : 1'bz;  // Controlled_Buffer controlled_buffer_14
  assign controlled_buffer_14_out = Program_Enable ? Program_Enable : 1'bz;  // Controlled_Buffer controlled_buffer_15
  assign controlled_buffer_16_out = not_5_out ? clock_2_out : 1'bz;  // Controlled_Buffer controlled_buffer_16
  not not_5 (not_5_out, controlled_buffer_14_out);
  ROM #(.dataWidth(4)) rom_2 (.addr(OutPut_Reg_q), .data(rom_2_data));
  assign controlled_buffer_7_out = rom_1_data[4] ? register_1_q : 8'bz;  // Controlled_Buffer controlled_buffer_17
  assign controlled_buffer_7_out = rom_1_data[6] ? register_2_q : 8'bz;  // Controlled_Buffer controlled_buffer_18
  Register OutPut_Reg (
    .D(controlled_buffer_7_out), .en(rom_1_data[0]), .clk(controlled_buffer_16_out), .Q(OutPut_Reg_q),
    .clr(Reset_computer));
  Register register_1 (
    .D(controlled_buffer_7_out), .en(rom_1_data[3]), .clk(controlled_buffer_16_out), .Q(register_1_q),
    .clr(Reset_computer));
  Adder adder_1 (.a(register_1_q), .b(register_2_q), .out(adder_1_out), .cout(nor_1_out[1]));  // open: cin
  Subtractor subtractor_1 (
    .a(register_1_q), .b(register_2_q), .out(subtractor_1_out), .bout(subtractor_1_bout));  // open: bin
  Register register_2 (
    .D(controlled_buffer_7_out), .en(rom_1_data[5]), .clk(controlled_buffer_16_out), .Q(register_2_q),
    .clr(Reset_computer));
  Hex_Digit_Display #(.decimalPoint("false")) hex_digit_display_3 (.value(rom_2_data));
  assign controlled_buffer_7_out = rom_1_data[2] ? multiplexer_3_out : 8'bz;  // Controlled_Buffer controlled_buffer_19
  Hex_Digit_Display #(.decimalPoint("false")) hex_digit_display_4 (.value(rom_3_data));
  Hex_Digit_Display #(.decimalPoint("false")) hex_digit_display_5 (.value(rom_4_data));
  ROM #(.dataWidth(4)) rom_3 (.addr(OutPut_Reg_q), .data(rom_3_data));
  Multiplexer #(.width(8)) multiplexer_3 (
    .in0(adder_1_out), .in1(subtractor_1_out), .out(multiplexer_3_out), .sel(rom_1_data[1]));
  Register #(.width(2)) register_3 (
    .D(nor_1_out), .en(rom_1_data[17]), .clk(controlled_buffer_16_out), .Q(register_3_q));  // open: clr
  ROM #(.dataWidth(4)) rom_4 (.addr(OutPut_Reg_q), .data(rom_4_data));
  nor nor_1 (nor_1_out[0], multiplexer_3_out[0], multiplexer_3_out[1], multiplexer_3_out[2], multiplexer_3_out[3], multiplexer_3_out[4], multiplexer_3_out[5], multiplexer_3_out[6], multiplexer_3_out[7]);

  // Notes on the sheet:
  //   contents of rom_1 (hex, n*v repeats v):
  //   16*10800 16*9200 900 900 900 0 900 108 0 0 900 0 0 0 4100 0 11 80 1008 1020 1020 0 2010 0 0 0 1008
  //   8*0 c e 61*0 16*10800 16*9200 900 900 900 0 900 108 0 0 900 0 0 0 4100 0 11 80 1008 1020 1020 0 2010
  //   0 0 0 1008 8*0 c e 61*0 16*10800 16*9200 900 15*0 1008 79*0 16*10800 16*9200
  //   contents of rom_2 (hex, n*v repeats v):
  //   100*0 100*1 56*2
  //   Output_Decimal
  //   contents of rom_3 (hex, n*v repeats v):
  //   10*0 10*1 10*2 10*3 10*4 10*5 10*6 10*7 10*8 10*9 10*0 10*1 10*2 10*3 10*4 10*5 10*6 10*7 10*8 10*9
  //   10*0 10*1 10*2 10*3 10*4 6*5
  //   contents of rom_4 (hex, n*v repeats v):
  //   0 1 2 3 4 5 6 7 8 9 0 1 2 3 4 5 6 7 8 9 0 1 2 3 4 5 6 7 8 9 0 1 2 3 4 5 6 7 8 9 0 1 2 3 4 5 6 7 8 9
  //   0 1 2 3 4 5 6 7 8 9 0 1 2 3 4 5 6 7 8 9 0 1 2 3 4 5 6 7 8 9 0 1 2 3 4 5 6 7 8 9 0 1 2 3 4 5 6 7 8 9
  //   0 1 2 3 4 5 6 7 8 9 0 1 2 3 4 5 6 7 8 9 0 1 2 3 4 5 6 7 8 9 0 1 2 3 4 5 6 7 8 9 0 1 2 3 4 5 6 7 8 9
  //   0 1 2 3 4 5 6 7 8 9 0 1 2 3 4 5 6 7 8 9 0 1 2 3 4 5 6 7 8 9 0 1 2 3 4 5 6 7 8 9 0 1 2 3 4 5 6 7 8 9
  //   0 1 2 3 4 5 6 7 8 9 0 1 2 3 4 5 6 7 8 9 0 1 2 3 4 5 6 7 8 9 0 1 2 3 4 5 6 7 8 9 0 1 2 3 4 5 6 7 8 9
  //   0 1 2 3 4 5
endmodule
